# Fritzing sketch 1dpong (saved by Fritzing 0.9.3b)
breadboards: 1

parts:
  Bauteil1 = Arduino Nano (Rev3.0)
  R1 = Resistor [tolerance=±5% resistance=220 package=THT]
  C1 = Electrolytic Capacitor [capacitance=220µF package="100 mil [THT, electrolytic]"]
  S1 = Pushbutton [package="[THT]"]
  S2 = Pushbutton [package="[THT]"]
  S3 = Pushbutton [package="[THT]"]
  S4 = Pushbutton [package="[THT]"]
  SPKR1 = Loudspeaker
  U1 = WS2812 RGB LED strip
  U2 = WS2812 RGB LED strip
  U3 = WS2812 RGB LED strip

nets:
  GND: Bauteil1.GND, S1.Pin_1, S1.Pin_2, S2.Pin_1, S2.Pin_2, S3.Pin_1, S3.Pin_2, S4.Pin_1, S4.Pin_2, SPKR1.pin2, U1.GND, U2.GND, U3.GND
  N1: Bauteil1.D2, S1.Pin_3, S1.Pin_4
  N2: Bauteil1.D3, S2.Pin_3, S2.Pin_4
  N3: Bauteil1.D4, S3.Pin_3, S3.Pin_4
  N4: Bauteil1.D5, S4.Pin_3, S4.Pin_4
  N5: Bauteil1.D6, U3.DIN
  N6: Bauteil1.D7, U2.DIN
  N7: Bauteil1.D8, R1.Pin_0
  N8: Bauteil1.D9, U1.DIN
  5V: Bauteil1.VIN, U1.VCC, U2.VCC, U3.VCC
  N9: R1.Pin_1, C1.+
  N10: C1.-, SPKR1.pin1

custom parts:
  WS2812 RGB LED strip: WS2812 strip
